# Fritzing sketch sketch (saved by Fritzing 0.9.5d)

parts:
  Controller = NodeMCU V3.0
  R1 = Resistor [tolerance=±5% resistance=220 package="0805 [SMD]"]
  R2 = Resistor [tolerance=±5% resistance=220 package="0805 [SMD]"]
  R3 = Resistor [tolerance=±5% resistance=220 package="0805 [SMD]"]
  R4 = Resistor [tolerance=±5% resistance=220 package="0805 [SMD]"]
  R5 = Resistor [tolerance=±5% resistance=220 package="0805 [SMD]"]
  R6 = Resistor [tolerance=±5% resistance=220 package="0805 [SMD]"]
  R7 = Resistor [tolerance=±5% resistance=220 package="0805 [SMD]"]
  R8 = Resistor [tolerance=±5% resistance=220 package="0805 [SMD]"]
  IRF1405 = MOSFET-NCHANNEL [package=to-92]
  D2 = Rectifier Diode [part_number=1N4001 package="300 mil [THT]"]
  Vibromodule1 = Vibration Motor- ROB-08449 [package=vibe-motor-10mm]
  IRF1406 = MOSFET-NCHANNEL [package=to-92]
  1N4007 = Rectifier Diode [part_number=1N4007 package="300 mil [THT]"]
  Vibromodule = Vibration Motor- ROB-08449 [package=vibe-motor-10mm]
  IRF1407 = MOSFET-NCHANNEL [package=to-92]
  D4 = Rectifier Diode [part_number=1N4001 package="300 mil [THT]"]
  Vibromodule3 = Vibration Motor- ROB-08449 [package=vibe-motor-10mm]
  IRF1408 = MOSFET-NCHANNEL [package=to-92]
  D5 = Rectifier Diode [part_number=1N4001 package="300 mil [THT]"]
  Vibromodule4 = Vibration Motor- ROB-08449 [package=vibe-motor-10mm]
  IRF1409 = MOSFET-NCHANNEL [package=to-92]
  D6 = Rectifier Diode [part_number=1N4001 package="300 mil [THT]"]
  Vibromodule5 = Vibration Motor- ROB-08449 [package=vibe-motor-10mm]
  IRF1410 = MOSFET-NCHANNEL [package=to-92]
  IRF1411 = MOSFET-NCHANNEL [package=to-92]
  IRF1412 = MOSFET-NCHANNEL [package=to-92]
  D7 = Rectifier Diode [part_number=1N4001 package="300 mil [THT]"]
  D8 = Rectifier Diode [part_number=1N4001 package="300 mil [THT]"]
  D9 = Rectifier Diode [part_number=1N4001 package="300 mil [THT]"]
  Vibromodule6 = Vibration Motor- ROB-08449 [package=vibe-motor-10mm]
  Vibromodule7 = Vibration Motor- ROB-08449 [package=vibe-motor-10mm]
  Vibromodule8 = Vibration Motor- ROB-08449 [package=vibe-motor-10mm]
  U1 = SWITCH-SPST-2 [package=r_sw_th]

nets:
  N1: Controller.D0, R1.Pin_0
  N2: Controller.D1, R2.Pin_0
  N3: Controller.D2, R3.Pin_0
  N4: Controller.D3, R4.Pin_0
  N5: Controller.D4, R5.Pin_0
  N6: Controller.GND, IRF1405.S, IRF1407.S, IRF1408.S, IRF1409.S, IRF1410.S, IRF1412.S
  N7: Controller.D5, R6.Pin_0
  N8: Controller.D6, R7.Pin_0
  N9: Controller.D7, R8.Pin_0
  N10: Controller.3V3, U1.P
  N11: R1.Pin_1, IRF1406.G
  N12: R2.Pin_1, IRF1405.G
  N13: R3.Pin_1, IRF1407.G
  N14: R4.Pin_1, IRF1408.G
  N15: R5.Pin_1, IRF1409.G
  N16: R6.Pin_1, IRF1412.G
  N17: R7.Pin_1, IRF1410.G
  N18: R8.Pin_1, IRF1411.G
  N19: IRF1405.D, D2.anode, Vibromodule1.-
  N20: D2.cathode, Vibromodule1.+, 1N4007.cathode, Vibromodule.+, D4.cathode, Vibromodule3.+, D5.cathode, Vibromodule4.+, D6.cathode, Vibromodule5.+, D7.cathode, D8.cathode, D9.cathode, Vibromodule6.+, Vibromodule7.+, Vibromodule8.+, U1.O
  N21: IRF1406.D, 1N4007.anode, Vibromodule.-
  N22: IRF1407.D, D4.anode, Vibromodule3.-
  N23: IRF1408.D, D5.anode, Vibromodule4.-
  N24: IRF1409.D, D6.anode, Vibromodule5.-
  N25: IRF1410.D, D9.anode, Vibromodule6.-
  N26: IRF1411.D, D8.anode, Vibromodule8.-
  N27: IRF1412.D, D7.anode, Vibromodule7.-

custom parts:
  NodeMCU V3.0: ESP8266 based NodeMCU
